// Logisim project alu.circ as structural Verilog: 2 circuits, main circuit main
module main (
  input  [31:0] X,
  input  [31:0] Y,
  input  [3:0] Switch,
  output Signed_Overflow,
  output Equal,
  output [31:0] Result,
  output [31:0] Result_2
);

  wire and_2_out, and_3_out, comparator_1_lt, comparator_2_lt, comparator_3_eq, comparator_4_eq,
       overflow_1_overflow, overflow_2_overflow;
  wire [31:0] add_val, adder_2_out, and_1_out, bit_extender_1_out, bit_extender_2_out, demultiplexer_1_out0,
       demultiplexer_1_out1, demultiplexer_1_out2, demultiplexer_1_out3, demultiplexer_1_out4,
       demultiplexer_1_out5, demultiplexer_1_out6, demultiplexer_1_out7, demultiplexer_1_out8,
       demultiplexer_1_out9, demultiplexer_1_out10, demultiplexer_1_out11, demultiplexer_1_out12,
       divider_1_out, divider_1_rem, multiplier_1_cout, multiplier_1_out, or_1_out, shifter_1_out,
       shifter_2_out, shifter_3_out, sub_val, subtractor_2_out;

  Demultiplexer #(.select(4), .width(32)) demultiplexer_1 (
    .out0(demultiplexer_1_out0), .out1(demultiplexer_1_out1), .out2(demultiplexer_1_out2),
    .out3(demultiplexer_1_out3), .out4(demultiplexer_1_out4), .out5(demultiplexer_1_out5),
    .out6(demultiplexer_1_out6), .out7(demultiplexer_1_out7), .out8(demultiplexer_1_out8),
    .out9(demultiplexer_1_out9), .out10(demultiplexer_1_out10), .out11(demultiplexer_1_out11),
    .out12(demultiplexer_1_out12), .in(X), .sel(Switch));  // open: out13, out14, out15, en
  Shifter #(.width(32)) shifter_1 (.in(demultiplexer_1_out0), .\dist (Y[4:0]), .out(shifter_1_out));
  Shifter #(.width(32), .shift("lr")) shifter_2 (.in(demultiplexer_1_out1), .\dist (Y[4:0]), .out(shifter_2_out));
  Shifter #(.width(32), .shift("ar")) shifter_3 (.in(demultiplexer_1_out2), .\dist (Y[4:0]), .out(shifter_3_out));
  Multiplier #(.width(32)) multiplier_1 (
    .a(demultiplexer_1_out3), .b(Y), .out(multiplier_1_out), .cout(multiplier_1_cout));  // open: cin
  Divider #(.width(32)) divider_1 (
    .a(demultiplexer_1_out4), .b(Y), .out(divider_1_out), .rem(divider_1_rem));  // open: upper
  Adder #(.width(32)) adder_1 (.a(Y), .b(demultiplexer_1_out5), .out(add_val));  // open: cin, cout
  Adder #(.width(32)) adder_2 (.a(demultiplexer_1_out6), .b(Y), .out(adder_2_out));  // open: cin, cout
  Subtractor #(.width(32)) subtractor_1 (.a(demultiplexer_1_out7), .b(Y), .out(sub_val));  // open: bin, bout
  Subtractor #(.width(32)) subtractor_2 (.a(demultiplexer_1_out8), .b(Y), .out(subtractor_2_out));  // open: bin, bout
  assign and_1_out = demultiplexer_1_out9 & Y;  // AND_Gate and_1, 32 bits wide
  assign or_1_out = demultiplexer_1_out10 | Y;  // OR_Gate or_1, 32 bits wide
  Comparator #(.width(32)) comparator_1 (.a(demultiplexer_1_out11), .b(Y), .lt(comparator_1_lt));  // open: gt, eq
  Comparator #(.width(32)) comparator_2 (.a(Y), .b(demultiplexer_1_out12), .lt(comparator_2_lt));  // open: gt, eq
  assign bit_extender_1_out = {{31{1'b0}}, comparator_1_lt};  // Bit_Extender bit_extender_1
  assign bit_extender_2_out = {{31{1'b0}}, comparator_2_lt};  // Bit_Extender bit_extender_2
  Comparator #(.width(4)) comparator_3 (.a(Switch), .b(4'b0101), .eq(comparator_3_eq));  // open: gt, lt
  Comparator #(.width(4)) comparator_4 (.a(Switch), .b(4'b0111), .eq(comparator_4_eq));  // open: gt, lt
  Multiplexer #(.select(4), .width(32)) multiplexer_1 (
    .in0({32{1'b0}}), .in1({32{1'b0}}), .in2({32{1'b0}}), .in3(multiplier_1_cout), .in4(divider_1_rem),
    .in5({32{1'b0}}), .in6({32{1'b0}}), .in7({32{1'b0}}), .in8({32{1'b0}}), .in9({32{1'b0}}),
    .in10({32{1'b0}}), .in11({32{1'b0}}), .in12({32{1'b0}}), .in13({32{1'b0}}), .in14({32{1'b0}}),
    .in15({32{1'b0}}), .out(Result_2), .sel(Switch));  // open: en
  Multiplexer #(.select(4), .width(32)) multiplexer_2 (
    .in0(shifter_1_out), .in1(shifter_2_out), .in2(shifter_3_out), .in3(multiplier_1_out),
    .in4(divider_1_out), .in5(add_val), .in6(adder_2_out), .in7(sub_val), .in8(subtractor_2_out),
    .in9(and_1_out), .in10(or_1_out), .in11(bit_extender_1_out), .in12(bit_extender_2_out),
    .in13({32{1'b0}}), .in14({32{1'b0}}), .in15({32{1'b0}}), .out(Result), .sel(Switch));  // open: en
  Comparator #(.width(32)) comparator_5 (.a(Y), .b(X), .eq(Equal));  // open: gt, lt
  overflow overflow_1 (.x_bit(Y[31]), .y_bit(X[31]), .result_bit(add_val[31]), .overflow(overflow_1_overflow));
  overflow overflow_2 (.x_bit(Y[31]), .y_bit(X[31]), .result_bit(sub_val[31]), .overflow(overflow_2_overflow));
  and and_2 (and_2_out, overflow_1_overflow, comparator_3_eq);
  and and_3 (and_3_out, comparator_4_eq, overflow_2_overflow);
  or or_2 (Signed_Overflow, and_2_out, and_3_out);

  // Other names for the same wires on the sheet: overflow = Signed_Overflow; S[3:0] = Switch

  // Notes on the sheet:
  //   INPUTS to your circuit
  //   DON'T CHANGE THE LOCATIONS OF THE INPUTS AND OUTPUTS!
  //   OUTPUTS from your circuit
endmodule

module overflow (
  input  x_bit,
  input  y_bit,
  input  result_bit,
  output overflow
);

  wire and_1_out, and_2_out, and_3_out, and_4_out, not_1_out, not_2_out, not_3_out;

  not not_1 (not_1_out, x_bit);
  not not_2 (not_2_out, y_bit);
  and and_1 (and_1_out, x_bit, y_bit);
  not not_3 (not_3_out, result_bit);
  and and_2 (and_2_out, not_1_out, not_2_out);
  and and_3 (and_3_out, and_1_out, not_3_out);
  and and_4 (and_4_out, and_2_out, result_bit);
  or or_1 (overflow, and_3_out, and_4_out);
endmodule
