// Logisim project cpu.circ as structural Verilog: 2 circuits, main circuit main
// 32
module main (
  input  [31:0] INSTRUCTION,
  input  CLOCK,
  output [31:0] FETCH_ADDRESS,
  output [31:0] s0_Value,
  output [31:0] s1_Value,
  output [31:0] s2_Value,
  output [31:0] ra_Value,
  output [31:0] HI_Value,
  output [31:0] LO_Value
);

  wire ALUSrc, and_1_out, and_2_out, and_6_out, and_7_out, and_8_out, beq, bne, branch_taken,
       comparator_1_eq, comparator_2_eq, comparator_3_eq, comparator_4_eq, comparator_5_eq, comparator_6_eq,
       comparator_8_eq, comparator_9_eq, comparator_10_eq, comparator_11_eq, Equal, ExtOp, jal, jr_instruct,
       jump, kill, link, lui, main_2_signed_overflow, MemtoReg, MemWr, mfhi, mfhi_mflo, mflo, multu_divu,
       or_4_out, RegDst, RegWr, shift, swinc;
  wire [2:0] OpUnitCtr;
  wire [3:0] ALUctr;
  wire [4:0] multiplexer_5_out, multiplexer_6_out, multiplexer_7_out, multiplexer_8_out, multiplexer_9_out;
  wire [5:0] funct, opcode;
  wire [15:6] immediate16;
  wire [25:16] j_addr;
  wire [27:0] bit_extender_1_out, shifter_1_out;
  wire [31:0] adder_2_out, bit_extender_3_out, bit_extender_4_out, branch_addr, demultiplexer_1_out0,
       demultiplexer_1_out1, demultiplexer_2_out1, main_1_read_data_2, main_2_result_2, MEM_p6,
       multiplexer_1_out, multiplexer_2_out, multiplexer_3_out, multiplexer_4_out, multiplexer_10_out,
       multiplexer_11_out, multiplexer_12_out, multiplexer_13_out, multiplexer_14_out, multiplexer_15_out,
       multiplexer_17_out, multiplexer_18_out, multiplexer_19_out, PC_4, R_rs____SignExtImm, rs_addr, shamt,
       shifter_2_out;

  assign bit_extender_1_out = {{2{1'b0}}, {j_addr, immediate16, funct}};  // Bit_Extender bit_extender_1
  Adder #(.width(32)) adder_1 (.a(FETCH_ADDRESS), .b(32'h4), .out(PC_4));  // open: cin, cout
  Shifter #(.width(28)) shifter_1 (.in(bit_extender_1_out), .\dist (5'b00010), .out(shifter_1_out));
  Shifter #(.width(32)) shifter_2 (.in(branch_addr), .\dist (5'b00010), .out(shifter_2_out));
  Adder #(.width(32)) adder_2 (.a(FETCH_ADDRESS), .b(shifter_2_out), .out(adder_2_out));  // open: cin, cout
  and and_1 (and_1_out, bne, ~Equal);  // AND_Gate
  or branch (branch_taken, and_1_out, and_2_out);
  and and_2 (and_2_out, Equal, beq);
  control control_1 (
    .opcode(opcode), .funct(funct), .equal(Equal), .MemWr(MemWr), .RegDst(RegDst), .ALUSrc(ALUSrc),
    .ALUctr(ALUctr), .MemtoReg(MemtoReg), .link(link), .ExtOp(ExtOp), .RegWr(RegWr), .jump(jump), .beq(beq),
    .bne(bne), .OpUnitCtr(OpUnitCtr), .shift(shift));
  Multiplexer #(.width(32)) multiplexer_1 (
    .in0(PC_4), .in1(adder_2_out), .out(multiplexer_1_out), .sel(branch_taken));  // open: en
  Multiplexer #(.width(32)) multiplexer_2 (
    .in0(multiplexer_1_out), .in1({PC_4[31:28], shifter_1_out}), .out(multiplexer_2_out), .sel(jump));  // open: en
  Comparator #(.width(6)) comparator_1 (.a(funct), .b(6'b010000), .eq(comparator_1_eq));  // open: gt, lt
  and and_3 (mfhi, comparator_1_eq, comparator_2_eq);
  Comparator #(.width(6)) comparator_2 (.a(opcode), .b({6{1'b0}}), .eq(comparator_2_eq));  // open: gt, lt
  Comparator #(.width(6)) comparator_3 (.a(funct), .b(6'b010010), .eq(comparator_3_eq));  // open: gt, lt
  Comparator #(.width(6)) comparator_4 (.a(opcode), .b({6{1'b0}}), .eq(comparator_4_eq));  // open: gt, lt
  Comparator #(.width(6)) comparator_5 (.a(opcode), .b({6{1'b0}}), .eq(comparator_5_eq));  // open: gt, lt
  Comparator #(.width(6)) comparator_6 (.a(funct), .b(6'b001000), .eq(comparator_6_eq));  // open: gt, lt
  Register #(.width(32)) PC (.D(multiplexer_3_out), .Q(FETCH_ADDRESS), .clk(CLOCK));  // open: en, clr
  Multiplexer #(.width(32)) multiplexer_3 (
    .in0(multiplexer_2_out), .in1(rs_addr), .out(multiplexer_3_out), .sel(jr_instruct));  // open: en
  and and_4 (mflo, comparator_3_eq, comparator_4_eq);
  and and_5 (jr_instruct, comparator_5_eq, comparator_6_eq);
  or or_1 (mfhi_mflo, mfhi, mflo);
  Register #(.width(32)) pipeline (
    .D(multiplexer_4_out), .Q({opcode, j_addr, immediate16, funct}), .clk(CLOCK));  // open: en, clr
  Multiplexer #(.width(32)) multiplexer_4 (
    .in0(INSTRUCTION), .in1({32{1'b0}}), .out(multiplexer_4_out), .sel(kill));  // open: en
  assign shamt = {{27{1'b0}}, immediate16[10:6]};  // Bit_Extender bit_extender_2
  Comparator #(.width(6)) comparator_7 (.a(opcode), .b(6'b001111), .eq(lui));  // open: gt, lt
  Comparator #(.width(6)) comparator_8 (.a(funct), .b(6'b011001), .eq(comparator_8_eq));  // open: gt, lt
  Comparator #(.width(6)) comparator_9 (.a(opcode), .b({6{1'b0}}), .eq(comparator_9_eq));  // open: gt, lt
  Comparator #(.width(6)) comparator_10 (.a(funct), .b(6'b011011), .eq(comparator_10_eq));  // open: gt, lt
  Comparator #(.width(6)) comparator_11 (.a(opcode), .b({6{1'b0}}), .eq(comparator_11_eq));  // open: gt, lt
  Multiplexer #(.width(5)) multiplexer_5 (
    .in0(j_addr[20:16]), .in1(immediate16[15:11]), .out(multiplexer_5_out), .sel(RegDst));  // open: en
  and and_6 (and_6_out, comparator_8_eq, comparator_9_eq);
  and and_7 (and_7_out, comparator_10_eq, comparator_11_eq);
  Comparator #(.width(6)) comparator_12 (.a(opcode), .b(6'b101100), .eq(swinc));  // open: gt, lt
  Multiplexer #(.width(5)) multiplexer_6 (
    .in0(j_addr[25:21]), .in1(j_addr[20:16]), .out(multiplexer_6_out), .sel(shift));  // open: en
  or or_2 (multu_divu, and_6_out, and_7_out);
  Comparator #(.width(6)) comparator_13 (.a(opcode), .b(6'b000011), .eq(jal));  // open: gt, lt
  Multiplexer #(.width(5)) multiplexer_7 (
    .in0(multiplexer_5_out), .in1(j_addr[25:21]), .out(multiplexer_7_out), .sel(swinc));  // open: en
  or or_3 (kill, jump, jr_instruct, branch_taken);
  Multiplexer #(.width(5)) multiplexer_8 (
    .in0(multiplexer_6_out), .in1(j_addr[25:21]), .out(multiplexer_8_out), .sel(jr_instruct));  // open: en
  Multiplexer #(.width(5)) multiplexer_9 (
    .in0(multiplexer_7_out), .in1({5{1'b1}}), .out(multiplexer_9_out), .sel(or_4_out));  // open: en
  or or_4 (or_4_out, and_8_out, jal);
  and and_8 (and_8_out, branch_taken, link);
  Multiplexer #(.width(32)) multiplexer_10 (
    .in0(multiplexer_11_out), .in1(FETCH_ADDRESS), .out(multiplexer_10_out), .sel(or_4_out));  // open: en
  Multiplexer #(.width(32)) multiplexer_11 (
    .in0(multiplexer_12_out), .in1(R_rs____SignExtImm), .out(multiplexer_11_out), .sel(swinc));  // open: en
  Multiplexer #(.width(32)) multiplexer_12 (
    .in0(multiplexer_19_out), .in1(multiplexer_13_out), .out(multiplexer_12_out), .sel(mfhi_mflo));  // open: en
  Multiplexer #(.width(32)) multiplexer_13 (
    .in0(LO_Value), .in1(HI_Value), .out(multiplexer_13_out), .sel(mfhi));  // open: en
  regfile_main main_1 (
    .Read_Register_1(multiplexer_8_out), .Read_Register_2(j_addr[20:16]), .Write_Register(multiplexer_9_out),
    .Write_Data(multiplexer_10_out), .Write_Enable(RegWr), .Clock(CLOCK), .Read_Data_1(rs_addr),
    .Read_Data_2(main_1_read_data_2), .s0_Value(s0_Value), .s1_Value(s1_Value), .s2_Value(s2_Value),
    .ra_Value(ra_Value));
  assign bit_extender_3_out = {{16{1'b0}}, {immediate16, funct}};  // Bit_Extender bit_extender_3
  assign bit_extender_4_out = {{16{immediate16[15]}}, {immediate16, funct}};  // Bit_Extender bit_extender_4
  Multiplexer #(.width(32)) multiplexer_14 (
    .in0(rs_addr), .in1(branch_addr), .out(multiplexer_14_out), .sel(lui));  // open: en
  Multiplexer #(.width(32)) multiplexer_15 (
    .in0(main_1_read_data_2), .in1(branch_addr), .out(multiplexer_15_out), .sel(ALUSrc));  // open: en
  Multiplexer #(.width(32)) multiplexer_16 (
    .in0(bit_extender_3_out), .in1(bit_extender_4_out), .out(branch_addr), .sel(ExtOp));  // open: en
  Multiplexer #(.width(32)) multiplexer_17 (
    .in0(multiplexer_15_out), .in1(32'h10), .out(multiplexer_17_out), .sel(lui));  // open: en
  LED led_1 (.in(main_2_signed_overflow));
  Multiplexer #(.width(32)) multiplexer_18 (
    .in0(multiplexer_17_out), .in1(shamt), .out(multiplexer_18_out), .sel(shift));  // open: en
  alu_main main_2 (
    .Switch(ALUctr), .X(multiplexer_14_out), .Equal(Equal), .Result(R_rs____SignExtImm),
    .Signed_Overflow(main_2_signed_overflow), .Y(multiplexer_18_out), .Result_2(main_2_result_2));
  Demultiplexer #(.width(32)) demultiplexer_1 (
    .out0(demultiplexer_1_out0), .out1(demultiplexer_1_out1), .in(R_rs____SignExtImm), .sel(multu_divu));  // open: en
  Demultiplexer #(.width(32)) demultiplexer_2 (
    .out1(demultiplexer_2_out1), .in(main_2_result_2), .sel(multu_divu));  // open: out0, en
  Register #(.width(32)) LO (.D(demultiplexer_1_out1), .en(multu_divu), .Q(LO_Value), .clk(CLOCK));  // open: clr
  Register #(.width(32)) HI (.D(demultiplexer_2_out1), .en(multu_divu), .Q(HI_Value), .clk(CLOCK));  // open: clr
  // mem_main MEM: pin names not known; wires that end beside it: demultiplexer_1_out0, main_1_read_data_2, MemWr, CLOCK, OpUnitCtr, MEM_p6
  Multiplexer #(.width(32)) multiplexer_19 (
    .in0(demultiplexer_1_out0), .in1(MEM_p6), .out(multiplexer_19_out), .sel(MemtoReg));  // open: en

  // Other names for the same wires on the sheet: clk = CLOCK; fetch_addr[31:0] = FETCH_ADDRESS;
  //   PC[31:0] = FETCH_ADDRESS; HI[31:0] = HI_Value; immediate16[5:0] = funct; j_addr[15:0] = {immediate16, funct};
  //   jr[4:0] = j_addr[25:21]; rs_field[4:0] = j_addr[25:21]; LO[31:0] = LO_Value; ra[31:0] = ra_Value;
  //   s0[31:0] = s0_Value; s1[31:0] = s1_Value; s2[31:0] = s2_Value

  // Notes on the sheet:
  //   Output
  //   These are outputs/inputs from run.circ
  //   Inputs
  //   These are DEBUG/TEST outputs from your circuit.
endmodule

module control (
  input  [5:0] opcode,
  input  [5:0] funct,
  input  equal,
  output MemWr,
  output RegDst,
  output ALUSrc,
  output [3:0] ALUctr,
  output MemtoReg,
  output link,
  output ExtOp,
  output RegWr,
  output jump,
  output beq,
  output bne,
  output [2:0] OpUnitCtr,
  output shift
);

  wire _0_opcode, add, addi, addiu, addu, \and , and_20_out, and_21_out, and_22_out, and_23_out, and_24_out,
       and_25_out, and_26_out, and_27_out, and_28_out, and_29_out, and_30_out, and_31_out, and_32_out,
       and_33_out, and_34_out, and_35_out, and_69_out, andi, beq_t, beqal, divu, j, jal, jr, lb, lbu, lhu,
       lui, lw, mfhi, mflo, multu, \or , or_10_out, or_11_out, or_12_out, or_13_out, or_14_out, or_15_out,
       or_16_out, ori, sb, sh, sll, slt, slti, sltu, sra, srl, sub, subu, sw, swinc;
  wire [2:0] and_52_out, and_53_out, and_54_out, and_55_out, bit_extender_1_out, bit_extender_2_out,
       bit_extender_3_out, bit_extender_4_out, bit_extender_5_out, bit_extender_6_out, bit_extender_7_out,
       bit_extender_8_out, or_4_out, or_5_out, or_6_out;
  wire [3:0] and_56_out, and_57_out, and_58_out, and_59_out, and_60_out, and_61_out, and_62_out, and_63_out,
       and_64_out, and_65_out, and_66_out, and_67_out, and_68_out, bit_extender_9_out, bit_extender_10_out,
       bit_extender_11_out, bit_extender_12_out, bit_extender_13_out, bit_extender_14_out,
       bit_extender_15_out, bit_extender_16_out, bit_extender_17_out, bit_extender_18_out,
       bit_extender_19_out, bit_extender_20_out, bit_extender_21_out;
  wire [5:0] demultiplexer_1_out0, demultiplexer_1_out1, multiplexer_1_out;

  Comparator #(.width(6)) comparator_1 (.a(opcode), .b({6{1'b0}}), .eq(_0_opcode));  // open: gt, lt
  Multiplexer #(.width(6)) multiplexer_1 (
    .in0(opcode), .in1(funct), .out(multiplexer_1_out), .sel(_0_opcode));  // open: en
  Demultiplexer #(.width(6)) demultiplexer_1 (
    .out0(demultiplexer_1_out0), .out1(demultiplexer_1_out1), .in(multiplexer_1_out), .sel(_0_opcode));  // open: en
  and and_1 (j, ~demultiplexer_1_out0[0], demultiplexer_1_out0[1], ~demultiplexer_1_out0[2], ~demultiplexer_1_out0[3], ~demultiplexer_1_out0[4], ~demultiplexer_1_out0[5]);  // AND_Gate
  and and_2 (jal, demultiplexer_1_out0[0], demultiplexer_1_out0[1], ~demultiplexer_1_out0[2], ~demultiplexer_1_out0[3], ~demultiplexer_1_out0[4], ~demultiplexer_1_out0[5]);  // AND_Gate
  and and_3 (beq_t, ~demultiplexer_1_out0[0], ~demultiplexer_1_out0[1], demultiplexer_1_out0[2], ~demultiplexer_1_out0[3], ~demultiplexer_1_out0[4], ~demultiplexer_1_out0[5]);  // AND_Gate
  and and_4 (bne, demultiplexer_1_out0[0], ~demultiplexer_1_out0[1], demultiplexer_1_out0[2], ~demultiplexer_1_out0[3], ~demultiplexer_1_out0[4], ~demultiplexer_1_out0[5]);  // AND_Gate
  and and_5 (beqal, ~demultiplexer_1_out0[0], ~demultiplexer_1_out0[1], demultiplexer_1_out0[2], ~demultiplexer_1_out0[3], demultiplexer_1_out0[4], ~demultiplexer_1_out0[5]);  // AND_Gate
  and and_6 (addi, ~demultiplexer_1_out0[0], ~demultiplexer_1_out0[1], ~demultiplexer_1_out0[2], demultiplexer_1_out0[3], ~demultiplexer_1_out0[4], ~demultiplexer_1_out0[5]);  // AND_Gate
  and and_7 (addiu, demultiplexer_1_out0[0], ~demultiplexer_1_out0[1], ~demultiplexer_1_out0[2], demultiplexer_1_out0[3], ~demultiplexer_1_out0[4], ~demultiplexer_1_out0[5]);  // AND_Gate
  and and_8 (slti, ~demultiplexer_1_out0[0], demultiplexer_1_out0[1], ~demultiplexer_1_out0[2], demultiplexer_1_out0[3], ~demultiplexer_1_out0[4], ~demultiplexer_1_out0[5]);  // AND_Gate
  and and_9 (andi, ~demultiplexer_1_out0[0], ~demultiplexer_1_out0[1], demultiplexer_1_out0[2], demultiplexer_1_out0[3], ~demultiplexer_1_out0[4], ~demultiplexer_1_out0[5]);  // AND_Gate
  and and_10 (ori, demultiplexer_1_out0[0], ~demultiplexer_1_out0[1], demultiplexer_1_out0[2], demultiplexer_1_out0[3], ~demultiplexer_1_out0[4], ~demultiplexer_1_out0[5]);  // AND_Gate
  and and_11 (lui, demultiplexer_1_out0[0], demultiplexer_1_out0[1], demultiplexer_1_out0[2], demultiplexer_1_out0[3], ~demultiplexer_1_out0[4], ~demultiplexer_1_out0[5]);  // AND_Gate
  and and_12 (lb, ~demultiplexer_1_out0[0], ~demultiplexer_1_out0[1], ~demultiplexer_1_out0[2], ~demultiplexer_1_out0[3], ~demultiplexer_1_out0[4], demultiplexer_1_out0[5]);  // AND_Gate
  and and_13 (lw, demultiplexer_1_out0[0], demultiplexer_1_out0[1], ~demultiplexer_1_out0[2], ~demultiplexer_1_out0[3], ~demultiplexer_1_out0[4], demultiplexer_1_out0[5]);  // AND_Gate
  and and_14 (lbu, ~demultiplexer_1_out0[0], ~demultiplexer_1_out0[1], demultiplexer_1_out0[2], ~demultiplexer_1_out0[3], ~demultiplexer_1_out0[4], demultiplexer_1_out0[5]);  // AND_Gate
  and and_15 (lhu, demultiplexer_1_out0[0], ~demultiplexer_1_out0[1], demultiplexer_1_out0[2], ~demultiplexer_1_out0[3], ~demultiplexer_1_out0[4], demultiplexer_1_out0[5]);  // AND_Gate
  and and_16 (sb, ~demultiplexer_1_out0[0], ~demultiplexer_1_out0[1], ~demultiplexer_1_out0[2], demultiplexer_1_out0[3], ~demultiplexer_1_out0[4], demultiplexer_1_out0[5]);  // AND_Gate
  and and_17 (sh, demultiplexer_1_out0[0], ~demultiplexer_1_out0[1], ~demultiplexer_1_out0[2], demultiplexer_1_out0[3], ~demultiplexer_1_out0[4], demultiplexer_1_out0[5]);  // AND_Gate
  and and_18 (sw, demultiplexer_1_out0[0], demultiplexer_1_out0[1], ~demultiplexer_1_out0[2], demultiplexer_1_out0[3], ~demultiplexer_1_out0[4], demultiplexer_1_out0[5]);  // AND_Gate
  and and_19 (swinc, ~demultiplexer_1_out0[0], ~demultiplexer_1_out0[1], demultiplexer_1_out0[2], demultiplexer_1_out0[3], ~demultiplexer_1_out0[4], demultiplexer_1_out0[5]);  // AND_Gate
  and and_20 (and_20_out, ~demultiplexer_1_out1[0], ~demultiplexer_1_out1[1], ~demultiplexer_1_out1[2], ~demultiplexer_1_out1[3], ~demultiplexer_1_out1[4], ~demultiplexer_1_out1[5]);  // AND_Gate
  and and_21 (and_21_out, ~demultiplexer_1_out1[0], demultiplexer_1_out1[1], ~demultiplexer_1_out1[2], ~demultiplexer_1_out1[3], ~demultiplexer_1_out1[4], ~demultiplexer_1_out1[5]);  // AND_Gate
  and and_22 (and_22_out, demultiplexer_1_out1[0], demultiplexer_1_out1[1], ~demultiplexer_1_out1[2], ~demultiplexer_1_out1[3], ~demultiplexer_1_out1[4], ~demultiplexer_1_out1[5]);  // AND_Gate
  and and_23 (and_23_out, ~demultiplexer_1_out1[0], ~demultiplexer_1_out1[1], ~demultiplexer_1_out1[2], demultiplexer_1_out1[3], ~demultiplexer_1_out1[4], ~demultiplexer_1_out1[5]);  // AND_Gate
  and and_24 (and_24_out, ~demultiplexer_1_out1[0], ~demultiplexer_1_out1[1], ~demultiplexer_1_out1[2], ~demultiplexer_1_out1[3], demultiplexer_1_out1[4], ~demultiplexer_1_out1[5]);  // AND_Gate
  and and_25 (and_25_out, ~demultiplexer_1_out1[0], demultiplexer_1_out1[1], ~demultiplexer_1_out1[2], ~demultiplexer_1_out1[3], demultiplexer_1_out1[4], ~demultiplexer_1_out1[5]);  // AND_Gate
  and and_26 (and_26_out, demultiplexer_1_out1[0], ~demultiplexer_1_out1[1], ~demultiplexer_1_out1[2], demultiplexer_1_out1[3], demultiplexer_1_out1[4], ~demultiplexer_1_out1[5]);  // AND_Gate
  and and_27 (and_27_out, demultiplexer_1_out1[0], demultiplexer_1_out1[1], ~demultiplexer_1_out1[2], demultiplexer_1_out1[3], demultiplexer_1_out1[4], ~demultiplexer_1_out1[5]);  // AND_Gate
  and and_28 (and_28_out, ~demultiplexer_1_out1[0], ~demultiplexer_1_out1[1], ~demultiplexer_1_out1[2], ~demultiplexer_1_out1[3], ~demultiplexer_1_out1[4], demultiplexer_1_out1[5]);  // AND_Gate
  and and_29 (and_29_out, demultiplexer_1_out1[0], ~demultiplexer_1_out1[1], ~demultiplexer_1_out1[2], ~demultiplexer_1_out1[3], ~demultiplexer_1_out1[4], demultiplexer_1_out1[5]);  // AND_Gate
  and and_30 (and_30_out, ~demultiplexer_1_out1[0], demultiplexer_1_out1[1], ~demultiplexer_1_out1[2], ~demultiplexer_1_out1[3], ~demultiplexer_1_out1[4], demultiplexer_1_out1[5]);  // AND_Gate
  and and_31 (and_31_out, demultiplexer_1_out1[0], demultiplexer_1_out1[1], ~demultiplexer_1_out1[2], ~demultiplexer_1_out1[3], ~demultiplexer_1_out1[4], demultiplexer_1_out1[5]);  // AND_Gate
  and and_32 (and_32_out, ~demultiplexer_1_out1[0], ~demultiplexer_1_out1[1], demultiplexer_1_out1[2], ~demultiplexer_1_out1[3], ~demultiplexer_1_out1[4], demultiplexer_1_out1[5]);  // AND_Gate
  and and_33 (and_33_out, demultiplexer_1_out1[0], ~demultiplexer_1_out1[1], demultiplexer_1_out1[2], ~demultiplexer_1_out1[3], ~demultiplexer_1_out1[4], demultiplexer_1_out1[5]);  // AND_Gate
  and and_34 (and_34_out, ~demultiplexer_1_out1[0], demultiplexer_1_out1[1], ~demultiplexer_1_out1[2], demultiplexer_1_out1[3], ~demultiplexer_1_out1[4], demultiplexer_1_out1[5]);  // AND_Gate
  and and_35 (and_35_out, demultiplexer_1_out1[0], demultiplexer_1_out1[1], ~demultiplexer_1_out1[2], demultiplexer_1_out1[3], ~demultiplexer_1_out1[4], demultiplexer_1_out1[5]);  // AND_Gate
  and and_36 (sll, _0_opcode, and_20_out);
  and and_37 (srl, _0_opcode, and_21_out);
  and and_38 (sra, _0_opcode, and_22_out);
  and and_39 (jr, _0_opcode, and_23_out);
  and and_40 (mfhi, _0_opcode, and_24_out);
  and and_41 (mflo, _0_opcode, and_25_out);
  and and_42 (multu, _0_opcode, and_26_out);
  and and_43 (divu, _0_opcode, and_27_out);
  and and_44 (add, _0_opcode, and_28_out);
  and and_45 (addu, _0_opcode, and_29_out);
  and and_46 (sub, _0_opcode, and_30_out);
  and and_47 (subu, _0_opcode, and_31_out);
  and and_48 (\and , _0_opcode, and_32_out);
  and and_49 (\or , _0_opcode, and_33_out);
  and and_50 (slt, _0_opcode, and_34_out);
  and and_51 (sltu, _0_opcode, and_35_out);
  or or_1 (shift, sll, sra, srl);
  or or_2 (RegDst, sll, srl, sra, \and , \or , add, addu, sub, subu, slt, sltu, mfhi, mflo);
  assign bit_extender_1_out = {{2{lbu}}, lbu};  // Bit_Extender bit_extender_1
  assign bit_extender_2_out = {{2{sb}}, sb};  // Bit_Extender bit_extender_2
  assign bit_extender_3_out = {{2{lhu}}, lhu};  // Bit_Extender bit_extender_3
  assign bit_extender_4_out = {{2{sh}}, sh};  // Bit_Extender bit_extender_4
  assign bit_extender_5_out = {{2{lw}}, lw};  // Bit_Extender bit_extender_5
  assign bit_extender_6_out = {{2{sw}}, sw};  // Bit_Extender bit_extender_6
  assign bit_extender_7_out = {{2{swinc}}, swinc};  // Bit_Extender bit_extender_7
  or or_3 (MemWr, sb, sh, sw, swinc);
  assign or_4_out = bit_extender_1_out | bit_extender_2_out;  // OR_Gate or_4, 3 bits wide
  assign bit_extender_8_out = {{2{lb}}, lb};  // Bit_Extender bit_extender_8
  assign or_5_out = bit_extender_3_out | bit_extender_4_out;  // OR_Gate or_5, 3 bits wide
  assign or_6_out = bit_extender_5_out | bit_extender_6_out | bit_extender_7_out;  // OR_Gate or_6, 3 bits wide
  or or_7 (MemtoReg, lb, lbu, lhu, lw);
  assign and_52_out = 3'b000 & or_4_out;  // AND_Gate and_52, 3 bits wide
  assign and_53_out = 3'b001 & bit_extender_8_out;  // AND_Gate and_53, 3 bits wide
  assign and_54_out = 3'b010 & or_5_out;  // AND_Gate and_54, 3 bits wide
  assign and_55_out = 3'b100 & or_6_out;  // AND_Gate and_55, 3 bits wide
  assign OpUnitCtr = and_52_out | and_53_out | and_54_out | and_55_out;  // OR_Gate or_8, 3 bits wide
  or or_9 (ALUSrc, addi, addiu, andi, lb, lhu, lbu, lui, lw, ori, slti, sb, sh, sw, swinc);
  or or_10 (or_10_out, sll, lui);
  or or_11 (or_11_out, add, addi, lb, lbu, lw, sb, sh, sw, swinc);
  or or_12 (or_12_out, addu, addiu);
  or or_13 (or_13_out, beq_t, bne, beqal, sub);
  or or_14 (or_14_out, \and , andi);
  or or_15 (or_15_out, \or , ori);
  or or_16 (or_16_out, slt, slti);
  assign bit_extender_9_out = {{3{or_10_out}}, or_10_out};  // Bit_Extender bit_extender_9
  assign bit_extender_10_out = {{3{srl}}, srl};  // Bit_Extender bit_extender_10
  assign bit_extender_11_out = {{3{sra}}, sra};  // Bit_Extender bit_extender_11
  assign bit_extender_12_out = {{3{multu}}, multu};  // Bit_Extender bit_extender_12
  assign bit_extender_13_out = {{3{divu}}, divu};  // Bit_Extender bit_extender_13
  assign bit_extender_14_out = {{3{or_11_out}}, or_11_out};  // Bit_Extender bit_extender_14
  assign bit_extender_15_out = {{3{or_12_out}}, or_12_out};  // Bit_Extender bit_extender_15
  assign bit_extender_16_out = {{3{or_13_out}}, or_13_out};  // Bit_Extender bit_extender_16
  assign bit_extender_17_out = {{3{subu}}, subu};  // Bit_Extender bit_extender_17
  assign bit_extender_18_out = {{3{or_14_out}}, or_14_out};  // Bit_Extender bit_extender_18
  assign bit_extender_19_out = {{3{or_15_out}}, or_15_out};  // Bit_Extender bit_extender_19
  assign bit_extender_20_out = {{3{or_16_out}}, or_16_out};  // Bit_Extender bit_extender_20
  assign bit_extender_21_out = {{3{sltu}}, sltu};  // Bit_Extender bit_extender_21
  assign and_56_out = 4'b0000 & bit_extender_9_out;  // AND_Gate and_56, 4 bits wide
  assign and_57_out = 4'b0001 & bit_extender_10_out;  // AND_Gate and_57, 4 bits wide
  assign and_58_out = 4'b0010 & bit_extender_11_out;  // AND_Gate and_58, 4 bits wide
  assign and_59_out = 4'b0011 & bit_extender_12_out;  // AND_Gate and_59, 4 bits wide
  assign and_60_out = 4'b0100 & bit_extender_13_out;  // AND_Gate and_60, 4 bits wide
  assign and_61_out = 4'b0101 & bit_extender_14_out;  // AND_Gate and_61, 4 bits wide
  assign and_62_out = 4'b0110 & bit_extender_15_out;  // AND_Gate and_62, 4 bits wide
  assign and_63_out = 4'b0111 & bit_extender_16_out;  // AND_Gate and_63, 4 bits wide
  assign and_64_out = 4'b1000 & bit_extender_17_out;  // AND_Gate and_64, 4 bits wide
  assign and_65_out = 4'b1001 & bit_extender_18_out;  // AND_Gate and_65, 4 bits wide
  assign and_66_out = 4'b1010 & bit_extender_19_out;  // AND_Gate and_66, 4 bits wide
  assign and_67_out = 4'b1011 & bit_extender_20_out;  // AND_Gate and_67, 4 bits wide
  assign and_68_out = 4'b1100 & bit_extender_21_out;  // AND_Gate and_68, 4 bits wide
  assign ALUctr = and_56_out | and_57_out | and_58_out | and_59_out | and_60_out | and_61_out | and_62_out | and_63_out | and_64_out | and_65_out | and_66_out | and_67_out | and_68_out;  // OR_Gate or_17, 4 bits wide
  and and_69 (and_69_out, beqal, equal);
  or or_18 (RegWr, addi, addiu, slti, andi, ori, lui, lb, lw, lbu, lhu, sll, srl, sra, add, addu, sub, subu, \and , \or , slt, sltu, mfhi, mflo, swinc, jal, and_69_out);
  or or_19 (ExtOp, addi, addiu, beq_t, lb, lhu, lbu, bne, lw, beqal, slti, sb, sh, sw, swinc);
  or or_20 (link, jal, beqal);
  or or_21 (jump, j, jal);
  or or_22 (beq, beq_t, beqal);
endmodule
