// Logisim project regfile.circ as structural Verilog: 33 circuits, main circuit main
module main (
  input  [4:0] Read_Register_1,
  input  [4:0] Read_Register_2,
  input  [4:0] Write_Register,
  input  [31:0] Write_Data,
  input  Write_Enable,
  input  Clock,
  output [31:0] s0_Value,
  output [31:0] s1_Value,
  output [31:0] s2_Value,
  output [31:0] ra_Value,
  output [31:0] Read_Data_1,
  output [31:0] Read_Data_2
);

  wire [31:0] _0, a0, a1, a2, a3, at, fp, gp, k0, k1, s3, s4, s5, s6, s7, sp, t0, t1, t2, t3, t4, t5, t6, t7,
       t8, t9, v0, v1;

  Multiplexer #(.select(5), .width(32)) multiplexer_1 (
    .in0(_0), .in1(at), .in2(v0), .in3(v1), .in4(a0), .in5(a1), .in6(a2), .in7(a3), .in8(t0), .in9(t1),
    .in10(t2), .in11(t3), .in12(t4), .in13(t5), .in14(t6), .in15(t7), .in16(s0_Value), .in17(s1_Value),
    .in18(s2_Value), .in19(s3), .in20(s4), .in21(s5), .in22(s6), .in23(s7), .in24(t8), .in25(t9), .in26(k0),
    .in27(k1), .in28(k1), .in29(sp), .in30(fp), .in31(ra_Value), .out(Read_Data_2), .sel(Read_Register_2));  // open: en
  Multiplexer #(.select(5), .width(32)) multiplexer_2 (
    .in0(_0), .in1(at), .in2(v0), .in3(v1), .in4(a0), .in5(a1), .in6(a2), .in7(a3), .in8(t0), .in9(t1),
    .in10(t2), .in11(t3), .in12(t4), .in13(t5), .in14(t6), .in15(t7), .in16(s0_Value), .in17(s1_Value),
    .in18(s2_Value), .in19(s3), .in20(s4), .in21(s5), .in22(s6), .in23(s7), .in24(t8), .in25(t9), .in26(k0),
    .in27(k1), .in28(k1), .in29(sp), .in30(fp), .in31(ra_Value), .out(Read_Data_1), .sel(Read_Register_1));  // open: en
  _0 u_0_1 (
    .Write_Data(Write_Data), .Write_Register(Write_Register), .Write_Enable(Write_Enable), .Clock(Clock),
    .Read_Data(_0));
  s1 s1_1 (
    .Write_Data(Write_Data), .Write_Register(Write_Register), .Write_Enable(Write_Enable), .Clock(Clock),
    .Read_Data(s1_Value));
  s2 s2_1 (
    .Write_Data(Write_Data), .Write_Register(Write_Register), .Write_Enable(Write_Enable), .Clock(Clock),
    .Read_Data(s2_Value));
  s3 s3_1 (
    .Write_Data(Write_Data), .Write_Register(Write_Register), .Write_Enable(Write_Enable), .Clock(Clock),
    .Read_Data(s3));
  at at_1 (
    .Write_Data(Write_Data), .Write_Register(Write_Register), .Write_Enable(Write_Enable), .Clock(Clock),
    .Read_Data(at));
  v0 v0_1 (
    .Write_Data(Write_Data), .Write_Register(Write_Register), .Write_Enable(Write_Enable), .Clock(Clock),
    .Read_Data(v0));
  s4 s4_1 (
    .Write_Data(Write_Data), .Write_Register(Write_Register), .Write_Enable(Write_Enable), .Clock(Clock),
    .Read_Data(s4));
  s5 s5_1 (
    .Write_Data(Write_Data), .Write_Register(Write_Register), .Write_Enable(Write_Enable), .Clock(Clock),
    .Read_Data(s5));
  s6 s6_1 (
    .Write_Data(Write_Data), .Write_Register(Write_Register), .Write_Enable(Write_Enable), .Clock(Clock),
    .Read_Data(s6));
  s7 s7_1 (
    .Write_Data(Write_Data), .Write_Register(Write_Register), .Write_Enable(Write_Enable), .Clock(Clock),
    .Read_Data(s7));
  t8 t8_1 (
    .Write_Data(Write_Data), .Write_Register(Write_Register), .Write_Enable(Write_Enable), .Clock(Clock),
    .Read_Data(t8));
  t9 t9_1 (
    .Write_Data(Write_Data), .Write_Register(Write_Register), .Write_Enable(Write_Enable), .Clock(Clock),
    .Read_Data(t9));
  k0 k0_1 (
    .Write_Data(Write_Data), .Write_Register(Write_Register), .Write_Enable(Write_Enable), .Clock(Clock),
    .Read_Data(k0));
  k1 k1_1 (
    .Write_Data(Write_Data), .Write_Register(Write_Register), .Write_Enable(Write_Enable), .Clock(Clock),
    .Read_Data(k1));
  gp gp_1 (
    .Write_Data(Write_Data), .Write_Register(Write_Register), .Write_Enable(Write_Enable), .Clock(Clock),
    .Read_Data(gp));
  sp sp_1 (
    .Write_Data(Write_Data), .Write_Register(Write_Register), .Write_Enable(Write_Enable), .Clock(Clock),
    .Read_Data(sp));
  ra ra_1 (
    .Write_Data(Write_Data), .Write_Register(Write_Register), .Write_Enable(Write_Enable), .Clock(Clock),
    .Read_Data(ra_Value));
  v1 v1_1 (
    .Write_Data(Write_Data), .Write_Register(Write_Register), .Write_Enable(Write_Enable), .Clock(Clock),
    .Read_Data(v1));
  fp fp_1 (
    .Write_Data(Write_Data), .Write_Register(Write_Register), .Write_Enable(Write_Enable), .Clock(Clock),
    .Read_Data(fp));
  a2 a2_1 (
    .Write_Data(Write_Data), .Write_Register(Write_Register), .Write_Enable(Write_Enable), .Clock(Clock),
    .Read_Data(a2));
  t6 t6_1 (
    .Write_Data(Write_Data), .Write_Register(Write_Register), .Write_Enable(Write_Enable), .Clock(Clock),
    .Read_Data(t6));
  a0 a0_1 (
    .Write_Data(Write_Data), .Write_Register(Write_Register), .Write_Enable(Write_Enable), .Clock(Clock),
    .Read_Data(a0));
  a1 a1_1 (
    .Write_Data(Write_Data), .Write_Register(Write_Register), .Write_Enable(Write_Enable), .Clock(Clock),
    .Read_Data(a1));
  a3 a3_1 (
    .Write_Data(Write_Data), .Write_Register(Write_Register), .Write_Enable(Write_Enable), .Clock(Clock),
    .Read_Data(a3));
  t2 t2_1 (
    .Write_Data(Write_Data), .Write_Register(Write_Register), .Write_Enable(Write_Enable), .Clock(Clock),
    .Read_Data(t2));
  t5 t5_1 (
    .Write_Data(Write_Data), .Write_Register(Write_Register), .Write_Enable(Write_Enable), .Clock(Clock),
    .Read_Data(t5));
  s0 s0_1 (
    .Write_Data(Write_Data), .Write_Register(Write_Register), .Write_Enable(Write_Enable), .Clock(Clock),
    .Read_Data(s0_Value));
  t0 t0_1 (
    .Write_Data(Write_Data), .Write_Register(Write_Register), .Write_Enable(Write_Enable), .Clock(Clock),
    .Read_Data(t0));
  t1 t1_1 (
    .Write_Data(Write_Data), .Write_Register(Write_Register), .Write_Enable(Write_Enable), .Clock(Clock),
    .Read_Data(t1));
  t3 t3_1 (
    .Write_Data(Write_Data), .Write_Register(Write_Register), .Write_Enable(Write_Enable), .Clock(Clock),
    .Read_Data(t3));
  t4 t4_1 (
    .Write_Data(Write_Data), .Write_Register(Write_Register), .Write_Enable(Write_Enable), .Clock(Clock),
    .Read_Data(t4));
  t7 t7_1 (
    .Write_Data(Write_Data), .Write_Register(Write_Register), .Write_Enable(Write_Enable), .Clock(Clock),
    .Read_Data(t7));

  // Other names for the same wires on the sheet: clk = Clock; ra[31:0] = ra_Value; read_data1[31:0] = Read_Data_1;
  //   read_data2[31:0] = Read_Data_2; read_reg1[4:0] = Read_Register_1; read_reg2[4:0] = Read_Register_2;
  //   s0[31:0] = s0_Value; s1[31:0] = s1_Value; s2[31:0] = s2_Value; write_en = Write_Enable;
  //   write_reg[4:0] = Write_Register

  // Notes on the sheet:
  //   INPUTS to your circuit
  //   DON'T CHANGE THE LOCATIONS OF THE INPUTS AND OUTPUTS!
  //   These are DEBUG/TEST outputs from your circuit.
  //   OUTPUTS from your circuit
endmodule

module _0 (
  input  [31:0] Write_Data,
  input  [4:0] Write_Register,
  input  Clock,
  input  Write_Enable,
  output [31:0] Read_Data
);

  wire and_1_out, and_2_out, not_1_out, not_2_out, not_3_out, not_4_out, not_5_out, xor_1_out;

  not not_1 (not_1_out, Write_Register[0]);
  not not_2 (not_2_out, Write_Register[1]);
  not not_3 (not_3_out, Write_Register[2]);
  not not_4 (not_4_out, Write_Register[3]);
  not not_5 (not_5_out, Write_Register[4]);
  and and_1 (and_1_out, not_1_out, not_2_out, not_3_out, not_4_out, not_5_out);
  xor xor_1 (xor_1_out, Write_Enable, Write_Enable);
  and and_2 (and_2_out, and_1_out, xor_1_out);
  Register #(.width(32)) register_1 (.D(Write_Data), .en(and_2_out), .Q(Read_Data), .clk(Clock));  // open: clr
endmodule

module at (
  input  [31:0] Write_Data,
  input  [4:0] Write_Register,
  input  Clock,
  input  Write_Enable,
  output [31:0] Read_Data
);

  wire and_1_out, and_2_out, not_1_out, not_2_out, not_3_out, not_4_out;

  not not_1 (not_1_out, Write_Register[1]);
  not not_2 (not_2_out, Write_Register[2]);
  not not_3 (not_3_out, Write_Register[3]);
  not not_4 (not_4_out, Write_Register[4]);
  and and_1 (and_1_out, Write_Register[0], not_1_out, not_2_out, not_3_out, not_4_out);
  and and_2 (and_2_out, and_1_out, Write_Enable);
  Register #(.width(32)) register_1 (.D(Write_Data), .en(and_2_out), .Q(Read_Data), .clk(Clock));  // open: clr
endmodule

module v0 (
  input  [31:0] Write_Data,
  input  [4:0] Write_Register,
  input  Clock,
  input  Write_Enable,
  output [31:0] Read_Data
);

  wire and_1_out, and_2_out, not_1_out, not_2_out, not_3_out, not_4_out;

  not not_1 (not_1_out, Write_Register[0]);
  not not_2 (not_2_out, Write_Register[2]);
  not not_3 (not_3_out, Write_Register[3]);
  not not_4 (not_4_out, Write_Register[4]);
  and and_1 (and_1_out, not_1_out, Write_Register[1], not_2_out, not_3_out, not_4_out);
  and and_2 (and_2_out, and_1_out, Write_Enable);
  Register #(.width(32)) register_1 (.D(Write_Data), .en(and_2_out), .Q(Read_Data), .clk(Clock));  // open: clr
endmodule

module v1 (
  input  [31:0] Write_Data,
  input  [4:0] Write_Register,
  input  Clock,
  input  Write_Enable,
  output [31:0] Read_Data
);

  wire and_1_out, and_2_out, not_1_out, not_2_out, not_3_out;

  not not_1 (not_1_out, Write_Register[2]);
  not not_2 (not_2_out, Write_Register[3]);
  not not_3 (not_3_out, Write_Register[4]);
  and and_1 (and_1_out, Write_Register[0], Write_Register[1], not_1_out, not_2_out, not_3_out);
  and and_2 (and_2_out, and_1_out, Write_Enable);
  Register #(.width(32)) register_1 (.D(Write_Data), .en(and_2_out), .Q(Read_Data), .clk(Clock));  // open: clr
endmodule

module a0 (
  input  [31:0] Write_Data,
  input  [4:0] Write_Register,
  input  Clock,
  input  Write_Enable,
  output [31:0] Read_Data
);

  wire and_1_out, and_2_out, not_1_out, not_2_out, not_3_out, not_4_out;

  not not_1 (not_1_out, Write_Register[0]);
  not not_2 (not_2_out, Write_Register[1]);
  not not_3 (not_3_out, Write_Register[3]);
  not not_4 (not_4_out, Write_Register[4]);
  and and_1 (and_1_out, not_1_out, not_2_out, Write_Register[2], not_3_out, not_4_out);
  and and_2 (and_2_out, and_1_out, Write_Enable);
  Register #(.width(32)) register_1 (.D(Write_Data), .en(and_2_out), .Q(Read_Data), .clk(Clock));  // open: clr
endmodule

module a1 (
  input  [31:0] Write_Data,
  input  [4:0] Write_Register,
  input  Clock,
  input  Write_Enable,
  output [31:0] Read_Data
);

  wire and_1_out, and_2_out, not_1_out, not_2_out, not_3_out;

  not not_1 (not_1_out, Write_Register[1]);
  not not_2 (not_2_out, Write_Register[3]);
  not not_3 (not_3_out, Write_Register[4]);
  and and_1 (and_1_out, Write_Register[0], not_1_out, Write_Register[2], not_2_out, not_3_out);
  and and_2 (and_2_out, and_1_out, Write_Enable);
  Register #(.width(32)) register_1 (.D(Write_Data), .en(and_2_out), .Q(Read_Data), .clk(Clock));  // open: clr
endmodule

module a2 (
  input  [31:0] Write_Data,
  input  [4:0] Write_Register,
  input  Clock,
  input  Write_Enable,
  output [31:0] Read_Data
);

  wire and_1_out, and_2_out, not_1_out, not_2_out, not_3_out;

  not not_1 (not_1_out, Write_Register[0]);
  not not_2 (not_2_out, Write_Register[3]);
  not not_3 (not_3_out, Write_Register[4]);
  and and_1 (and_1_out, not_1_out, Write_Register[1], Write_Register[2], not_2_out, not_3_out);
  and and_2 (and_2_out, and_1_out, Write_Enable);
  Register #(.width(32)) register_1 (.D(Write_Data), .en(and_2_out), .Q(Read_Data), .clk(Clock));  // open: clr
endmodule

module a3 (
  input  [31:0] Write_Data,
  input  [4:0] Write_Register,
  input  Clock,
  input  Write_Enable,
  output [31:0] Read_Data
);

  wire and_1_out, and_2_out, not_1_out, not_2_out;

  not not_1 (not_1_out, Write_Register[3]);
  not not_2 (not_2_out, Write_Register[4]);
  and and_1 (and_1_out, Write_Register[0], Write_Register[1], Write_Register[2], not_1_out, not_2_out);
  and and_2 (and_2_out, and_1_out, Write_Enable);
  Register #(.width(32)) register_1 (.D(Write_Data), .en(and_2_out), .Q(Read_Data), .clk(Clock));  // open: clr
endmodule

module t0 (
  input  [31:0] Write_Data,
  input  [4:0] Write_Register,
  input  Clock,
  input  Write_Enable,
  output [31:0] Read_Data
);

  wire and_1_out, and_2_out, not_1_out, not_2_out, not_3_out, not_4_out;

  not not_1 (not_1_out, Write_Register[0]);
  not not_2 (not_2_out, Write_Register[1]);
  not not_3 (not_3_out, Write_Register[2]);
  not not_4 (not_4_out, Write_Register[4]);
  and and_1 (and_1_out, not_1_out, not_2_out, not_3_out, Write_Register[3], not_4_out);
  and and_2 (and_2_out, and_1_out, Write_Enable);
  Register #(.width(32)) register_1 (.D(Write_Data), .en(and_2_out), .Q(Read_Data), .clk(Clock));  // open: clr
endmodule

module t1 (
  input  [31:0] Write_Data,
  input  [4:0] Write_Register,
  input  Clock,
  input  Write_Enable,
  output [31:0] Read_Data
);

  wire and_1_out, and_2_out, not_1_out, not_2_out, not_3_out;

  not not_1 (not_1_out, Write_Register[1]);
  not not_2 (not_2_out, Write_Register[2]);
  not not_3 (not_3_out, Write_Register[4]);
  and and_1 (and_1_out, Write_Register[0], not_1_out, not_2_out, Write_Register[3], not_3_out);
  and and_2 (and_2_out, and_1_out, Write_Enable);
  Register #(.width(32)) register_1 (.D(Write_Data), .en(and_2_out), .Q(Read_Data), .clk(Clock));  // open: clr
endmodule

module t2 (
  input  [31:0] Write_Data,
  input  [4:0] Write_Register,
  input  Clock,
  input  Write_Enable,
  output [31:0] Read_Data
);

  wire and_1_out, and_2_out, not_1_out, not_2_out, not_3_out;

  not not_1 (not_1_out, Write_Register[0]);
  not not_2 (not_2_out, Write_Register[2]);
  not not_3 (not_3_out, Write_Register[4]);
  and and_1 (and_1_out, not_1_out, Write_Register[1], not_2_out, Write_Register[3], not_3_out);
  and and_2 (and_2_out, and_1_out, Write_Enable);
  Register #(.width(32)) register_1 (.D(Write_Data), .en(and_2_out), .Q(Read_Data), .clk(Clock));  // open: clr
endmodule

module t3 (
  input  [31:0] Write_Data,
  input  [4:0] Write_Register,
  input  Clock,
  input  Write_Enable,
  output [31:0] Read_Data
);

  wire and_1_out, and_2_out, not_1_out, not_2_out;

  not not_1 (not_1_out, Write_Register[2]);
  not not_2 (not_2_out, Write_Register[4]);
  and and_1 (and_1_out, Write_Register[0], Write_Register[1], not_1_out, Write_Register[3], not_2_out);
  and and_2 (and_2_out, and_1_out, Write_Enable);
  Register #(.width(32)) register_1 (.D(Write_Data), .en(and_2_out), .Q(Read_Data), .clk(Clock));  // open: clr
endmodule

module t4 (
  input  [31:0] Write_Data,
  input  [4:0] Write_Register,
  input  Clock,
  input  Write_Enable,
  output [31:0] Read_Data
);

  wire and_1_out, and_2_out, not_1_out, not_2_out, not_3_out;

  not not_1 (not_1_out, Write_Register[0]);
  not not_2 (not_2_out, Write_Register[1]);
  not not_3 (not_3_out, Write_Register[4]);
  and and_1 (and_1_out, not_1_out, not_2_out, Write_Register[2], Write_Register[3], not_3_out);
  and and_2 (and_2_out, and_1_out, Write_Enable);
  Register #(.width(32)) register_1 (.D(Write_Data), .en(and_2_out), .Q(Read_Data), .clk(Clock));  // open: clr
endmodule

module t5 (
  input  [31:0] Write_Data,
  input  [4:0] Write_Register,
  input  Clock,
  input  Write_Enable,
  output [31:0] Read_Data
);

  wire and_1_out, and_2_out, not_1_out, not_2_out;

  not not_1 (not_1_out, Write_Register[1]);
  not not_2 (not_2_out, Write_Register[4]);
  and and_1 (and_1_out, Write_Register[0], not_1_out, Write_Register[2], Write_Register[3], not_2_out);
  and and_2 (and_2_out, and_1_out, Write_Enable);
  Register #(.width(32)) register_1 (.D(Write_Data), .en(and_2_out), .Q(Read_Data), .clk(Clock));  // open: clr
endmodule

module t6 (
  input  [31:0] Write_Data,
  input  [4:0] Write_Register,
  input  Clock,
  input  Write_Enable,
  output [31:0] Read_Data
);

  wire and_1_out, and_2_out, not_1_out, not_2_out;

  not not_1 (not_1_out, Write_Register[0]);
  not not_2 (not_2_out, Write_Register[4]);
  and and_1 (and_1_out, not_1_out, Write_Register[1], Write_Register[2], Write_Register[3], not_2_out);
  and and_2 (and_2_out, and_1_out, Write_Enable);
  Register #(.width(32)) register_1 (.D(Write_Data), .en(and_2_out), .Q(Read_Data), .clk(Clock));  // open: clr
endmodule

module t7 (
  input  [31:0] Write_Data,
  input  [4:0] Write_Register,
  input  Clock,
  input  Write_Enable,
  output [31:0] Read_Data
);

  wire and_1_out, and_2_out, not_1_out;

  not not_1 (not_1_out, Write_Register[4]);
  and and_1 (and_1_out, Write_Register[0], Write_Register[1], Write_Register[2], Write_Register[3], not_1_out);
  and and_2 (and_2_out, and_1_out, Write_Enable);
  Register #(.width(32)) register_1 (.D(Write_Data), .en(and_2_out), .Q(Read_Data), .clk(Clock));  // open: clr
endmodule

module s0 (
  input  [31:0] Write_Data,
  input  [4:0] Write_Register,
  input  Clock,
  input  Write_Enable,
  output [31:0] Read_Data
);

  wire and_1_out, and_2_out, not_1_out, not_2_out, not_3_out, not_4_out;

  not not_1 (not_1_out, Write_Register[0]);
  not not_2 (not_2_out, Write_Register[1]);
  not not_3 (not_3_out, Write_Register[2]);
  not not_4 (not_4_out, Write_Register[3]);
  and and_1 (and_1_out, not_1_out, not_2_out, not_3_out, not_4_out, Write_Register[4]);
  and and_2 (and_2_out, and_1_out, Write_Enable);
  Register #(.width(32)) register_1 (.D(Write_Data), .en(and_2_out), .Q(Read_Data), .clk(Clock));  // open: clr
endmodule

module s1 (
  input  [31:0] Write_Data,
  input  [4:0] Write_Register,
  input  Clock,
  input  Write_Enable,
  output [31:0] Read_Data
);

  wire and_1_out, and_2_out, not_1_out, not_2_out, not_3_out;

  not not_1 (not_1_out, Write_Register[1]);
  not not_2 (not_2_out, Write_Register[2]);
  not not_3 (not_3_out, Write_Register[3]);
  and and_1 (and_1_out, Write_Register[0], not_1_out, not_2_out, not_3_out, Write_Register[4]);
  and and_2 (and_2_out, and_1_out, Write_Enable);
  Register #(.width(32)) register_1 (.D(Write_Data), .en(and_2_out), .Q(Read_Data), .clk(Clock));  // open: clr
endmodule

module s2 (
  input  [31:0] Write_Data,
  input  [4:0] Write_Register,
  input  Clock,
  input  Write_Enable,
  output [31:0] Read_Data
);

  wire and_1_out, and_2_out, not_1_out, not_2_out, not_3_out;

  not not_1 (not_1_out, Write_Register[1]);
  not not_2 (not_2_out, Write_Register[2]);
  not not_3 (not_3_out, Write_Register[3]);
  and and_1 (and_1_out, Write_Register[0], not_1_out, not_2_out, not_3_out, Write_Register[4]);
  and and_2 (and_2_out, and_1_out, Write_Enable);
  Register #(.width(32)) register_1 (.D(Write_Data), .en(and_2_out), .Q(Read_Data), .clk(Clock));  // open: clr
endmodule

module s3 (
  input  [31:0] Write_Data,
  input  [4:0] Write_Register,
  input  Clock,
  input  Write_Enable,
  output [31:0] Read_Data
);

  wire and_1_out, and_2_out, not_1_out, not_2_out;

  not not_1 (not_1_out, Write_Register[2]);
  not not_2 (not_2_out, Write_Register[3]);
  and and_1 (and_1_out, Write_Register[0], Write_Register[1], not_1_out, not_2_out, Write_Register[4]);
  and and_2 (and_2_out, and_1_out, Write_Enable);
  Register #(.width(32)) register_1 (.D(Write_Data), .en(and_2_out), .Q(Read_Data), .clk(Clock));  // open: clr
endmodule

module s4 (
  input  [31:0] Write_Data,
  input  [4:0] Write_Register,
  input  Clock,
  input  Write_Enable,
  output [31:0] Read_Data
);

  wire and_1_out, and_2_out, not_1_out, not_2_out, not_3_out;

  not not_1 (not_1_out, Write_Register[0]);
  not not_2 (not_2_out, Write_Register[1]);
  not not_3 (not_3_out, Write_Register[3]);
  and and_1 (and_1_out, not_1_out, not_2_out, Write_Register[2], not_3_out, Write_Register[4]);
  and and_2 (and_2_out, and_1_out, Write_Enable);
  Register #(.width(32)) register_1 (.D(Write_Data), .en(and_2_out), .Q(Read_Data), .clk(Clock));  // open: clr
endmodule

module s5 (
  input  [31:0] Write_Data,
  input  [4:0] Write_Register,
  input  Clock,
  input  Write_Enable,
  output [31:0] Read_Data
);

  wire and_1_out, and_2_out, not_1_out, not_2_out;

  not not_1 (not_1_out, Write_Register[1]);
  not not_2 (not_2_out, Write_Register[3]);
  and and_1 (and_1_out, Write_Register[0], not_1_out, Write_Register[2], not_2_out, Write_Register[4]);
  and and_2 (and_2_out, and_1_out, Write_Enable);
  Register #(.width(32)) register_1 (.D(Write_Data), .en(and_2_out), .Q(Read_Data), .clk(Clock));  // open: clr
endmodule

module s6 (
  input  [31:0] Write_Data,
  input  [4:0] Write_Register,
  input  Clock,
  input  Write_Enable,
  output [31:0] Read_Data
);

  wire and_1_out, and_2_out, not_1_out, not_2_out;

  not not_1 (not_1_out, Write_Register[0]);
  not not_2 (not_2_out, Write_Register[3]);
  and and_1 (and_1_out, not_1_out, Write_Register[1], Write_Register[2], not_2_out, Write_Register[4]);
  and and_2 (and_2_out, and_1_out, Write_Enable);
  Register #(.width(32)) register_1 (.D(Write_Data), .en(and_2_out), .Q(Read_Data), .clk(Clock));  // open: clr
endmodule

module s7 (
  input  [31:0] Write_Data,
  input  [4:0] Write_Register,
  input  Clock,
  input  Write_Enable,
  output [31:0] Read_Data
);

  wire and_1_out, and_2_out, not_1_out;

  not not_1 (not_1_out, Write_Register[3]);
  and and_1 (and_1_out, Write_Register[0], Write_Register[1], Write_Register[2], not_1_out, Write_Register[4]);
  and and_2 (and_2_out, and_1_out, Write_Enable);
  Register #(.width(32)) register_1 (.D(Write_Data), .en(and_2_out), .Q(Read_Data), .clk(Clock));  // open: clr
endmodule

module t8 (
  input  [31:0] Write_Data,
  input  [4:0] Write_Register,
  input  Clock,
  input  Write_Enable,
  output [31:0] Read_Data
);

  wire and_1_out, and_2_out, not_1_out, not_2_out, not_3_out;

  not not_1 (not_1_out, Write_Register[0]);
  not not_2 (not_2_out, Write_Register[1]);
  not not_3 (not_3_out, Write_Register[2]);
  and and_1 (and_1_out, not_1_out, not_2_out, not_3_out, Write_Register[3], Write_Register[4]);
  and and_2 (and_2_out, and_1_out, Write_Enable);
  Register #(.width(32)) register_1 (.D(Write_Data), .en(and_2_out), .Q(Read_Data), .clk(Clock));  // open: clr
endmodule

module t9 (
  input  [31:0] Write_Data,
  input  [4:0] Write_Register,
  input  Clock,
  input  Write_Enable,
  output [31:0] Read_Data
);

  wire and_1_out, and_2_out, not_1_out, not_2_out;

  not not_1 (not_1_out, Write_Register[1]);
  not not_2 (not_2_out, Write_Register[2]);
  and and_1 (and_1_out, Write_Register[0], not_1_out, not_2_out, Write_Register[3], Write_Register[4]);
  and and_2 (and_2_out, and_1_out, Write_Enable);
  Register #(.width(32)) register_1 (.D(Write_Data), .en(and_2_out), .Q(Read_Data), .clk(Clock));  // open: clr
endmodule

module k0 (
  input  [31:0] Write_Data,
  input  [4:0] Write_Register,
  input  Clock,
  input  Write_Enable,
  output [31:0] Read_Data
);

  wire and_1_out, and_2_out, not_1_out, not_2_out;

  not not_1 (not_1_out, Write_Register[0]);
  not not_2 (not_2_out, Write_Register[2]);
  and and_1 (and_1_out, not_1_out, Write_Register[1], not_2_out, Write_Register[3], Write_Register[4]);
  and and_2 (and_2_out, and_1_out, Write_Enable);
  Register #(.width(32)) register_1 (.D(Write_Data), .en(and_2_out), .Q(Read_Data), .clk(Clock));  // open: clr
endmodule

module k1 (
  input  [31:0] Write_Data,
  input  [4:0] Write_Register,
  input  Clock,
  input  Write_Enable,
  output [31:0] Read_Data
);

  wire and_1_out, and_2_out, not_1_out;

  not not_1 (not_1_out, Write_Register[2]);
  and and_1 (and_1_out, Write_Register[0], Write_Register[1], not_1_out, Write_Register[3], Write_Register[4]);
  and and_2 (and_2_out, and_1_out, Write_Enable);
  Register #(.width(32)) register_1 (.D(Write_Data), .en(and_2_out), .Q(Read_Data), .clk(Clock));  // open: clr
endmodule

module gp (
  input  [31:0] Write_Data,
  input  [4:0] Write_Register,
  input  Clock,
  input  Write_Enable,
  output [31:0] Read_Data
);

  wire and_1_out, and_2_out, not_1_out, not_2_out;

  not not_1 (not_1_out, Write_Register[0]);
  not not_2 (not_2_out, Write_Register[1]);
  and and_1 (and_1_out, not_1_out, not_2_out, Write_Register[2], Write_Register[3], Write_Register[4]);
  and and_2 (and_2_out, and_1_out, Write_Enable);
  Register #(.width(32)) register_1 (.D(Write_Data), .en(and_2_out), .Q(Read_Data), .clk(Clock));  // open: clr
endmodule

module sp (
  input  [31:0] Write_Data,
  input  [4:0] Write_Register,
  input  Clock,
  input  Write_Enable,
  output [31:0] Read_Data
);

  wire and_1_out, and_2_out, not_1_out;

  not not_1 (not_1_out, Write_Register[1]);
  and and_1 (and_1_out, Write_Register[0], not_1_out, Write_Register[2], Write_Register[3], Write_Register[4]);
  and and_2 (and_2_out, and_1_out, Write_Enable);
  Register #(.width(32)) register_1 (.D(Write_Data), .en(and_2_out), .Q(Read_Data), .clk(Clock));  // open: clr
endmodule

module fp (
  input  [31:0] Write_Data,
  input  [4:0] Write_Register,
  input  Clock,
  input  Write_Enable,
  output [31:0] Read_Data
);

  wire and_1_out, and_2_out, not_1_out;

  not not_1 (not_1_out, Write_Register[0]);
  and and_1 (and_1_out, not_1_out, Write_Register[1], Write_Register[2], Write_Register[3], Write_Register[4]);
  and and_2 (and_2_out, and_1_out, Write_Enable);
  Register #(.width(32)) register_1 (.D(Write_Data), .en(and_2_out), .Q(Read_Data), .clk(Clock));  // open: clr
endmodule

module ra (
  input  [31:0] Write_Data,
  input  [4:0] Write_Register,
  input  Clock,
  input  Write_Enable,
  output [31:0] Read_Data
);

  wire and_1_out, and_2_out;

  and and_1 (and_1_out, Write_Register[0], Write_Register[1], Write_Register[2], Write_Register[3], Write_Register[4]);
  and and_2 (and_2_out, and_1_out, Write_Enable);
  Register #(.width(32)) register_1 (.D(Write_Data), .en(and_2_out), .Q(Read_Data), .clk(Clock));  // open: clr
endmodule
